# Fritzing sketch VR_LDR_input (saved by Fritzing 0.7.5b)
breadboards: 1

parts:
  Arduino1 = Arduino
  R4 = Resistor [tolerance=±5% resistance=1k package=THT]
  R5 = Photocell (LDR) [package=THT]
  R6 = Rotary Potentiometer (Small) [maximum_resistance=100kΩ]
  R7 = Resistor [tolerance=±5% resistance=100 package=THT]

nets:
  GND: Arduino1.GND, R4.Pin_1, R6.leg1
  5V: Arduino1.+5V, R5.pin_1, R7.Pin_0
  N1: Arduino1.A0, R6.wiper
  N2: Arduino1.A1, R4.Pin_0, R5.pin_0
  N3: R6.leg2, R7.Pin_1
