# Fritzing sketch IR_Simple (saved by Fritzing 0.7.5b)
breadboards: 2

parts:
  Arduino1 = Arduino
  LED1 = LED - 5mm [color="Infrared (940nm)" package="5 mm [THT]"]
  R8 = Resistor [tolerance=±5% resistance=100 package=THT]
  Arduino2 = Arduino
  U1 = mystery part, 3 pins [chip_label=? spacing=300mil]

nets:
  GND: Arduino1.GND, R8.Pin_0
  N1: Arduino1.D3, LED1.anode
  5V: Arduino1.+5V
  N2: LED1.cathode, R8.Pin_1
  N3: Arduino2.D11, U1.pin3
  N4: Arduino2.+5V, U1.pin1
  N5: Arduino2.GND, U1.pin2

notes:
  IR Receiver
  IR Sender
