# Fritzing sketch IR_VR_SERVO (saved by Fritzing 0.7.5b)
breadboards: 2

parts:
  Arduino1 = Arduino
  R6 = Rotary Potentiometer (Small) [maximum_resistance=100kΩ]
  R7 = Resistor [tolerance=±5% resistance=100 package=THT]
  LED1 = LED - 5mm [color="Infrared (940nm)" package="5 mm [THT]"]
  R8 = Resistor [tolerance=±5% resistance=100 package=THT]
  Arduino2 = Arduino
  J1 = Basic Servo
  U1 = mystery part, 3 pins [chip_label=? spacing=300mil]

nets:
  GND: Arduino1.GND, R6.leg1, R8.Pin_0
  N1: Arduino1.D3, LED1.anode
  5V: Arduino1.+5V, R7.Pin_0
  N2: Arduino1.A0, R6.wiper
  N3: R6.leg2, R7.Pin_1
  N4: LED1.cathode, R8.Pin_1
  N5: Arduino2.D11, U1.pin3
  N6: Arduino2.D3, J1.pulse
  +5V: Arduino2.+5V, J1.vcc, U1.pin1
  GND_2: Arduino2.GND, J1.gnd, U1.pin2

notes:
  IR Receiver
  IR Sender
