# Fritzing sketch IR_VR_SERVO (saved by Fritzing 0.7.5b)
breadboards: 1

parts:
  Arduino1 = Arduino
  R6 = Rotary Potentiometer (Small) [maximum_resistance=100kΩ]
  R7 = Resistor [tolerance=±5% resistance=100 package=THT]
  LED1 = LED - 5mm [color="Infrared (940nm)" package="5 mm [THT]"]
  R8 = Resistor [tolerance=±5% resistance=100 package=THT]

nets:
  GND: Arduino1.GND, R6.leg1, R8.Pin_0
  N1: Arduino1.D3, LED1.anode
  5V: Arduino1.+5V, R7.Pin_0
  N2: Arduino1.A0, R6.wiper
  N3: R6.leg2, R7.Pin_1
  N4: LED1.cathode, R8.Pin_1
